# Fritzing sketch sketch_schematic (saved by Fritzing 0.9.3b)
circuit board: 8.46667cm x 5.64444cm
breadboards: 1

parts:
  Adafruit_HUZZAH_ESP8266_Breakout1 = Adafruit HUZZAH ESP8266 Breakout [part_number=2471]
  DHT1 = DHT22 Humidity and Temperature Sensor
  R1 = Resistor [tolerance=±5% resistance=220k package=THT]
  R2 = Resistor [tolerance=±5% resistance=1M package=THT]

nets:
  GND: Adafruit_HUZZAH_ESP8266_Breakout1.GND, DHT1.GND, R2.Pin_1
  N1: Adafruit_HUZZAH_ESP8266_Breakout1.V+, R1.Pin_0
  N2: Adafruit_HUZZAH_ESP8266_Breakout1.#12, DHT1.DATA
  N3: Adafruit_HUZZAH_ESP8266_Breakout1.#16, Adafruit_HUZZAH_ESP8266_Breakout1.RST
  N4: Adafruit_HUZZAH_ESP8266_Breakout1.A, R1.Pin_1, R2.Pin_0
  N5: Adafruit_HUZZAH_ESP8266_Breakout1.3V, DHT1.VDD
